# Fritzing sketch scheme (saved by Fritzing 1.0.2b)

parts:
  U1 = SK6812 RGBW LED Strip
  U2 = SK6812 RGBW LED Strip
  U3 = SK6812 RGBW LED Strip
  Part1 = Arduino Nano (Rev3.0) (ICSP)
  S1 = Toggle Switch [package=THT]
  S2 = Pushbutton [package="[SMD]"]

nets:
  N1: U1.GND#0, U2.Dout, U3.Din, U3.GND#3
  N2: U1.Din, U1.GND#3, U3.Dout
  N3: U1.+5V, U3.+5V#5
  GND: U2.GND#0, Part1.GND, Part1.VIN, Part1.RESET, S2.Pin_1, S2.Pin_2
  N4: U2.Din, U2.GND#3, U3.GND#0, Part1.D2
  N5: U2.+5V#2, S1.L1
  N6: U2.+5V#5, U3.+5V#2
  N7: Part1.D3, S2.Pin_3, S2.Pin_4
  N8: Part1.5V, S1.COM, S1.L2

custom parts:
  SK6812 RGBW LED Strip: SK6812 RGBW Strip
